# Fritzing sketch HondenvoederFritzing (saved by Fritzing 0.9.3b)
breadboards: 1

parts:
  Part1 = Arduino Uno (Rev3)  # not connected
  Part2 = Arduino Ethernet Shield (Rev3)
  Part3 = Arduino Uno (Rev3)
  J1 = Basic Servo
  hc-sr1 = hc-sr04

nets:
  GND: Part2.GND, Part3.GND, hc-sr1.GND
  N1: Part2.PWM_D9, J1.pulse
  N2: Part2.A4/SDA, Part3.A4/SDA
  N3: Part2.A5/SCL, Part3.A5/SCL
  N4: Part3.D4, hc-sr1.Trig
  N5: Part3.D5_PWM, hc-sr1.Echo
  5V: Part3.5V, hc-sr1.VCC

notes:
  [ External 7.4v power supply ]
